// Logisim project parte1_módulos de memória e cache.circ as structural Verilog: 1 circuit, main circuit main
module main (
  input  in_1,
  input  in_2,
  input  in_3,
  input  in_4,
  input  [5:0] in_5,
  input  [7:0] in_6,
  input  Entrada_de_dados,
  input  in_8,
  input  in_9,
  output [7:0] out_10,
  output [7:0] out_11,
  output CS_ROM,
  output [7:0] out_13,
  output [2:0] out_14,
  output out_15,
  output [7:0] out_16,
  output [7:0] out_17,
  output out_18,
  output out_19,
  output out_20,
  output [2:0] out_21
);

  wire and_1_out, and_2_out, and_3_out, and_4_out, and_5_out, and_6_out, and_7_out, and_8_out, and_9_out,
       and_10_out, and_11_out, and_12_out, and_13_out, and_14_out, and_15_out, and_16_out, and_17_out,
       and_18_out, and_19_out, and_20_out, and_21_out, and_22_out, and_23_out, and_24_out, and_25_out,
       and_26_out, and_27_out, and_28_out, and_29_out, and_30_out, and_31_out, and_32_out, and_33_out,
       and_34_out, and_35_out, and_36_out, and_37_out, and_38_out, and_39_out, and_40_out, and_41_out,
       and_42_out, and_43_out, and_44_out, and_45_out, and_46_out, and_47_out, and_48_out, and_49_out,
       and_50_out, and_51_out, and_52_out, and_53_out, clock_2_out, clock_3_out, clock_4_out, clock_5_out,
       clock_6_out, clock_7_out, clock_8_out, clock_9_out, clock_10_out, clock_11_out, clock_12_out,
       clock_13_out, clock_14_out, clock_15_out, comparator_1_eq, comparator_2_eq, comparator_3_eq,
       comparator_4_eq, decoder_1_out2, decoder_1_out3, decoder_1_out4, decoder_1_out5, decoder_1_out6,
       decoder_1_out7, decoder_2_out1, decoder_2_out2, decoder_2_out3, decoder_3_out0, decoder_3_out1,
       decoder_3_out2, decoder_3_out3, decoder_4_out0, decoder_4_out1, decoder_4_out2, decoder_4_out3,
       decoder_4_out4, decoder_4_out5, decoder_4_out6, decoder_4_out7, decoder_4_out8, decoder_4_out9,
       decoder_4_out10, decoder_4_out11, decoder_4_out12, decoder_4_out13, decoder_4_out14, decoder_4_out15,
       j_k_ff_1_qn, j_k_ff_2_qn, not_1_out, not_2_out, not_3_out, not_4_out, not_5_out, not_6_out, not_7_out,
       not_8_out, not_9_out, not_10_out, not_11_out, not_12_out, not_13_out, not_14_out, not_15_out,
       not_16_out, not_17_out, not_18_out, not_19_out, not_21_out, not_22_out, not_23_out, not_24_out,
       not_25_out, not_26_out, not_27_out, not_28_out, not_29_out, not_30_out, not_31_out, not_32_out,
       or_1_out, or_2_out, or_3_out, or_4_out, or_5_out, or_6_out, or_7_out, or_8_out, or_9_out, or_10_out,
       or_11_out, or_12_out, or_13_out, or_14_out, or_15_out, or_16_out, or_17_out, or_18_out, or_19_out,
       ram_3_dout, register_14_q, register_15_q, register_16_q, xor_1_out, xor_2_out, xor_3_out, xor_4_out,
       xor_5_out;
  wire [2:0] j_k_ff_1_q, register_3_q, register_5_q;
  wire [3:0] multiplexer_1_out;
  wire [7:0] adder_1_out, bit_extender_1_out, multiplexer_2_out, multiplexer_3_out, multiplexer_4_out,
       multiplexer_5_out, multiplexer_6_out, ram_2_dout, register_4_q, register_6_q, register_8_q,
       register_9_q, register_10_q, register_11_q, register_12_q, register_17_q, register_18_q,
       register_19_q, register_20_q, register_21_q, register_22_q, register_23_q, register_24_q,
       register_25_q, register_26_q, register_27_q, register_28_q, register_29_q, register_30_q,
       register_31_q, register_32_q, rom_1_data;

  Clock clock_1 ();  // open: out
  Clock clock_2 (.out(clock_2_out));
  J_K_Flip_Flop j_k_ff_1 (
    .J(not_30_out), .K(not_30_out), .clk(clock_2_out), .Q(j_k_ff_1_q[0]), .Qn(j_k_ff_1_qn),
    .reset(decoder_1_out7));  // open: preset
  J_K_Flip_Flop j_k_ff_2 (
    .J(not_30_out), .K(not_30_out), .clk(j_k_ff_1_qn), .Q(j_k_ff_1_q[1]), .Qn(j_k_ff_2_qn),
    .reset(decoder_1_out7));  // open: preset
  J_K_Flip_Flop j_k_ff_3 (
    .J(not_30_out), .K(not_30_out), .clk(j_k_ff_2_qn), .Q(j_k_ff_1_q[2]), .reset(decoder_1_out7));  // open: Qn, preset
  Decoder #(.select(3)) decoder_1 (
    .out2(decoder_1_out2), .out3(decoder_1_out3), .out4(decoder_1_out4), .out5(decoder_1_out5),
    .out6(decoder_1_out6), .out7(decoder_1_out7), .sel(j_k_ff_1_q));  // open: out0, out1, en
  or or_1 (or_1_out, decoder_1_out3, decoder_1_out4);
  Decoder #(.enable("false"), .select(2)) decoder_2 (
    .out0(CS_ROM), .out1(decoder_2_out1), .out2(decoder_2_out2), .out3(decoder_2_out3), .sel(in_5[5:4]));
  Decoder #(.select(2)) decoder_3 (
    .out0(decoder_3_out0), .out1(decoder_3_out1), .out2(decoder_3_out2), .out3(decoder_3_out3),
    .sel(in_5[2:1]));  // open: en
  and and_1 (and_1_out, decoder_1_out5, and_2_out);
  and and_2 (and_2_out, decoder_3_out0, not_30_out);
  and and_3 (and_3_out, decoder_1_out2, and_2_out);
  and and_4 (and_4_out, decoder_3_out1, not_30_out);
  and and_5 (and_5_out, decoder_3_out2, not_30_out);
  and and_6 (and_6_out, decoder_3_out3, not_30_out);
  and and_7 (and_7_out, decoder_1_out6, and_2_out);
  and and_8 (and_8_out, decoder_1_out4, and_2_out);
  and and_9 (and_9_out, decoder_1_out6, and_4_out);
  and and_10 (and_10_out, decoder_1_out4, and_4_out);
  and and_11 (and_11_out, decoder_1_out6, and_5_out);
  and and_12 (and_12_out, decoder_1_out4, and_5_out);
  and and_13 (and_13_out, decoder_1_out6, and_6_out);
  and and_14 (and_14_out, decoder_1_out4, and_6_out);
  and and_15 (and_15_out, decoder_1_out5, and_4_out);
  and and_16 (and_16_out, decoder_1_out5, and_6_out);
  and and_17 (and_17_out, decoder_1_out2, and_4_out);
  and and_18 (and_18_out, decoder_1_out5, and_5_out);
  and and_19 (and_19_out, decoder_1_out2, and_5_out);
  and and_20 (and_20_out, decoder_1_out2, and_6_out);
  Comparator #(.width(2)) comparator_1 (.a(in_5[2:1]), .b(2'b00), .eq(comparator_1_eq));  // open: gt, lt
  Comparator #(.width(2)) comparator_2 (.a(in_5[2:1]), .b(2'b01), .eq(comparator_2_eq));  // open: gt, lt
  Comparator #(.width(2)) comparator_3 (.a(in_5[2:1]), .b(2'b10), .eq(comparator_3_eq));  // open: gt, lt
  Comparator #(.width(2)) comparator_4 (.a(in_5[2:1]), .b(2'b11), .eq(comparator_4_eq));  // open: gt, lt
  assign bit_extender_1_out = {{4{1'b0}}, in_5[3:0]};  // Bit_Extender bit_extender_1
  Register #(.width(3)) register_1 (.D(in_5[5:3]), .en(and_1_out), .clk(clock_3_out), .Q(out_14), .clr(in_4));
  Clock clock_3 (.out(clock_3_out));
  Register register_2 (.D(out_17), .en(and_3_out), .clk(clock_9_out), .Q(out_16), .clr(in_4));
  Register #(.width(3)) register_3 (.D(in_5[5:3]), .en(and_15_out), .clk(clock_10_out), .Q(register_3_q), .clr(in_4));
  Register register_4 (.D(out_17), .en(and_17_out), .clk(clock_4_out), .Q(register_4_q), .clr(in_4));
  Clock clock_4 (.out(clock_4_out));
  Register #(.width(3)) register_5 (.D(in_5[5:3]), .en(and_18_out), .clk(clock_5_out), .Q(register_5_q), .clr(in_4));
  Clock clock_5 (.out(clock_5_out));
  Register register_6 (.D(out_17), .en(and_19_out), .clk(clock_6_out), .Q(register_6_q), .clr(in_4));
  Clock clock_6 (.out(clock_6_out));
  Register #(.width(3)) register_7 (.D(in_5[5:3]), .en(and_16_out), .clk(clock_7_out), .Q(out_21), .clr(in_4));
  Clock clock_7 (.out(clock_7_out));
  Register register_8 (.D(out_17), .en(and_20_out), .clk(clock_8_out), .Q(register_8_q), .clr(in_4));
  Clock clock_8 (.out(clock_8_out));
  Adder adder_1 (.a(bit_extender_1_out), .b(8'h1), .out(adder_1_out));  // open: cin, cout
  Register register_9 (.D(out_17), .en(and_8_out), .clk(clock_9_out), .Q(register_9_q), .clr(in_4));
  Clock clock_9 (.out(clock_9_out));
  Register register_10 (.D(out_17), .en(and_10_out), .clk(clock_4_out), .Q(register_10_q), .clr(in_4));
  Register register_11 (.D(out_17), .en(and_12_out), .clk(clock_6_out), .Q(register_11_q), .clr(in_4));
  Register register_12 (.D(out_17), .en(and_14_out), .clk(clock_8_out), .Q(register_12_q), .clr(in_4));
  Multiplexer #(.width(4)) multiplexer_1 (
    .in0(in_5[3:0]), .in1(adder_1_out[3:0]), .out(multiplexer_1_out), .sel(or_1_out));
  assign out_11 = Entrada_de_dados ? in_6 : 8'bz;  // Controlled_Buffer controlled_buffer_1
  Register #(.width(1)) register_13 (.D(1'b1), .en(and_7_out), .clk(clock_3_out), .Q(out_15), .clr(in_4));
  Register #(.width(1)) register_14 (.D(1'b1), .en(and_9_out), .clk(clock_10_out), .Q(register_14_q), .clr(in_4));
  Clock clock_10 (.out(clock_10_out));
  Register #(.width(1)) register_15 (.D(1'b1), .en(and_11_out), .clk(clock_5_out), .Q(register_15_q), .clr(in_4));
  Register #(.width(1)) register_16 (.D(1'b1), .en(and_13_out), .clk(clock_7_out), .Q(register_16_q), .clr(in_4));
  not not_1 (not_1_out, in_5[5]);
  not not_2 (not_2_out, out_14[2]);
  not not_3 (not_3_out, in_5[4]);
  not not_4 (not_4_out, out_14[1]);
  not not_5 (not_5_out, in_5[3]);
  not not_6 (not_6_out, out_14[0]);
  Multiplexer #(.width(8)) multiplexer_2 (.in0(out_16), .in1(register_9_q), .out(multiplexer_2_out), .sel(in_5[0]));
  not not_7 (not_7_out, in_5[5]);
  not not_8 (not_8_out, register_3_q[2]);
  not not_9 (not_9_out, in_5[4]);
  not not_10 (not_10_out, register_3_q[1]);
  not not_11 (not_11_out, in_5[3]);
  not not_12 (not_12_out, register_3_q[0]);
  Multiplexer #(.width(8)) multiplexer_3 (
    .in0(register_4_q), .in1(register_10_q), .out(multiplexer_3_out), .sel(in_5[0]));
  not not_13 (not_13_out, in_5[5]);
  not not_14 (not_14_out, register_5_q[2]);
  not not_15 (not_15_out, in_5[4]);
  not not_16 (not_16_out, register_5_q[1]);
  not not_17 (not_17_out, in_5[3]);
  not not_18 (not_18_out, register_5_q[0]);
  Multiplexer #(.width(8)) multiplexer_4 (
    .in0(register_6_q), .in1(register_11_q), .out(multiplexer_4_out), .sel(in_5[0]));
  not not_19 (not_19_out, in_5[5]);
  // NOT_Gate not_20 has open pins: in=out_21[2], out=open
  not not_21 (not_21_out, in_5[4]);
  not not_22 (not_22_out, out_21[1]);
  not not_23 (not_23_out, in_5[3]);
  not not_24 (not_24_out, out_21[0]);
  Multiplexer #(.width(8)) multiplexer_5 (
    .in0(register_8_q), .in1(register_12_q), .out(multiplexer_5_out), .sel(in_5[0]));
  and and_21 (and_21_out, not_1_out, out_14[2]);
  and and_22 (and_22_out, in_5[5], not_2_out);
  and and_23 (and_23_out, not_3_out, out_14[1]);
  and and_24 (and_24_out, in_5[4], not_4_out);
  and and_25 (and_25_out, not_5_out, out_14[0]);
  and and_26 (and_26_out, in_5[3], not_6_out);
  and and_27 (and_27_out, not_7_out, register_3_q[2]);
  and and_28 (and_28_out, in_5[5], not_8_out);
  and and_29 (and_29_out, not_9_out, register_3_q[1]);
  and and_30 (and_30_out, in_5[4], not_10_out);
  and and_31 (and_31_out, not_11_out, register_3_q[0]);
  and and_32 (and_32_out, in_5[3], not_12_out);
  and and_33 (and_33_out, not_13_out, register_5_q[2]);
  and and_34 (and_34_out, in_5[5], not_14_out);
  and and_35 (and_35_out, not_15_out, register_5_q[1]);
  and and_36 (and_36_out, in_5[4], not_16_out);
  and and_37 (and_37_out, not_17_out, register_5_q[0]);
  and and_38 (and_38_out, in_5[3], not_18_out);
  and and_39 (and_39_out, not_19_out, out_21[2]);
  buf and_40 (and_40_out, in_5[5]);  // AND_Gate
  and and_41 (and_41_out, not_21_out, out_21[1]);
  and and_42 (and_42_out, in_5[4], not_22_out);
  and and_43 (and_43_out, not_23_out, out_21[0]);
  and and_44 (and_44_out, in_5[3], not_24_out);
  and and_45 (and_45_out, decoder_2_out3, in_2);
  or or_2 (or_2_out, and_21_out, and_22_out);
  or or_3 (or_3_out, and_23_out, and_24_out);
  or or_4 (or_4_out, and_25_out, and_26_out);
  or or_5 (or_5_out, and_27_out, and_28_out);
  or or_6 (or_6_out, and_29_out, and_30_out);
  or or_7 (or_7_out, and_31_out, and_32_out);
  or or_8 (or_8_out, and_33_out, and_34_out);
  or or_9 (or_9_out, and_35_out, and_36_out);
  or or_10 (or_10_out, and_37_out, and_38_out);
  or or_11 (or_11_out, and_39_out, and_40_out);
  or or_12 (or_12_out, and_41_out, and_42_out);
  or or_13 (or_13_out, and_43_out, and_44_out);
  not not_25 (not_25_out, Entrada_de_dados);
  or or_14 (or_14_out, or_2_out, or_3_out, or_4_out);
  not not_26 (not_26_out, or_14_out);
  or or_15 (or_15_out, or_5_out, or_6_out, or_7_out);
  not not_27 (not_27_out, or_15_out);
  or or_16 (or_16_out, or_8_out, or_9_out, or_10_out);
  not not_28 (not_28_out, or_16_out);
  or or_17 (or_17_out, or_11_out, or_12_out, or_13_out);
  not not_29 (not_29_out, or_17_out);
  and and_46 (and_46_out, decoder_2_out1, not_25_out);
  Decoder #(.select(4)) decoder_4 (
    .out0(decoder_4_out0), .out1(decoder_4_out1), .out2(decoder_4_out2), .out3(decoder_4_out3),
    .out4(decoder_4_out4), .out5(decoder_4_out5), .out6(decoder_4_out6), .out7(decoder_4_out7),
    .out8(decoder_4_out8), .out9(decoder_4_out9), .out10(decoder_4_out10), .out11(decoder_4_out11),
    .out12(decoder_4_out12), .out13(decoder_4_out13), .out14(decoder_4_out14), .out15(decoder_4_out15),
    .sel(in_5[3:0]), .en(decoder_2_out2));
  and and_47 (and_47_out, not_26_out, out_15, comparator_1_eq);
  assign out_17 = and_47_out ? multiplexer_2_out : 8'bz;  // Controlled_Buffer controlled_buffer_2
  and and_48 (and_48_out, not_27_out, register_14_q, comparator_2_eq);
  assign out_17 = and_48_out ? multiplexer_3_out : 8'bz;  // Controlled_Buffer controlled_buffer_3
  and and_49 (and_49_out, not_28_out, register_15_q, comparator_3_eq);
  assign out_17 = and_49_out ? multiplexer_4_out : 8'bz;  // Controlled_Buffer controlled_buffer_4
  and and_50 (and_50_out, not_29_out, register_16_q, comparator_4_eq);
  assign out_17 = and_50_out ? multiplexer_5_out : 8'bz;  // Controlled_Buffer controlled_buffer_5
  Register register_17 (.D(out_11), .en(decoder_4_out0), .clk(clock_11_out), .Q(register_17_q), .clr(in_1));
  Register register_18 (.D(out_11), .en(decoder_4_out15), .clk(clock_11_out), .Q(register_18_q), .clr(in_1));
  Clock clock_11 (.out(clock_11_out));
  and and_51 (and_51_out, Entrada_de_dados, decoder_2_out1);
  Clock clock_12 (.out(clock_12_out));
  Register register_19 (.D(out_11), .en(decoder_4_out14), .clk(clock_11_out), .Q(register_19_q), .clr(in_1));
  RAM #(.addrWidth(4)) ram_1 (
    .addr(multiplexer_1_out), .we(and_51_out), .oe(and_46_out), .clk(clock_12_out), .din(out_11),
    .dout(out_10));
  Register register_20 (.D(out_11), .en(decoder_4_out1), .clk(clock_11_out), .Q(register_20_q), .clr(in_1));
  Register register_21 (.D(out_11), .en(decoder_4_out2), .clk(clock_11_out), .Q(register_21_q), .clr(in_1));
  Register register_22 (.D(out_11), .en(decoder_4_out13), .clk(clock_11_out), .Q(register_22_q), .clr(in_1));
  ROM #(.addrWidth(4)) rom_1 (.addr(in_5[3:0]), .data(rom_1_data));
  xor xor_1 (xor_1_out, out_11[0], out_11[1], out_11[2], out_11[3], out_11[4], out_11[5], out_11[6], out_11[7]);
  Register register_23 (.D(out_11), .en(decoder_4_out3), .clk(clock_11_out), .Q(register_23_q), .clr(in_1));
  Register register_24 (.D(out_11), .en(decoder_4_out12), .clk(clock_11_out), .Q(register_24_q), .clr(in_1));
  Clock clock_13 (.out(clock_13_out));
  or or_18 (or_18_out, and_47_out, and_48_out, and_49_out, and_50_out);
  not not_30 (not_30_out, or_18_out);
  not not_31 (not_31_out, xor_1_out);
  Register register_25 (.D(out_11), .en(decoder_4_out4), .clk(clock_11_out), .Q(register_25_q), .clr(in_1));
  Register register_26 (.D(out_11), .en(decoder_4_out11), .clk(clock_11_out), .Q(register_26_q), .clr(in_1));
  RAM #(.addrWidth(4)) ram_2 (
    .addr(in_5[3:0]), .we(and_45_out), .oe(in_3), .clk(clock_13_out), .din(out_11), .dout(ram_2_dout));
  Clock clock_14 (.out(clock_14_out));
  Register register_27 (.D(out_11), .en(decoder_4_out10), .clk(clock_11_out), .Q(register_27_q), .clr(in_1));
  RAM #(.addrWidth(4), .dataWidth(1)) ram_3 (
    .addr(multiplexer_1_out), .we(and_51_out), .oe(and_46_out), .clk(clock_14_out), .din(not_31_out),
    .dout(ram_3_dout));
  Register register_28 (.D(out_11), .en(decoder_4_out5), .clk(clock_11_out), .Q(register_28_q), .clr(in_1));
  Register register_29 (.D(out_11), .en(decoder_4_out6), .clk(clock_11_out), .Q(register_29_q), .clr(in_1));
  Register register_30 (.D(out_11), .en(decoder_4_out9), .clk(clock_11_out), .Q(register_30_q), .clr(in_1));
  Register register_31 (.D(out_11), .en(decoder_4_out7), .clk(clock_11_out), .Q(register_31_q), .clr(in_1));
  Register register_32 (.D(out_11), .en(decoder_4_out8), .clk(clock_11_out), .Q(register_32_q), .clr(in_1));
  Clock clock_15 (.out(clock_15_out));
  xor xor_2 (xor_2_out, out_10[0], out_10[1], out_10[2], out_10[3], out_10[4], out_10[5], out_10[6], out_10[7]);
  not not_32 (not_32_out, xor_2_out);
  D_Flip_Flop d_ff_1 (.D(xor_3_out), .clk(clock_15_out), .Q(out_18), .reset(in_8));  // open: Qn, preset
  xor xor_3 (xor_3_out, or_18_out, out_18);
  D_Flip_Flop d_ff_2 (.D(xor_5_out), .clk(clock_15_out), .Q(out_19));  // open: Qn, preset, reset
  xor xor_4 (xor_4_out, ram_3_dout, not_32_out);
  LED led_1 (.in(xor_4_out));
  Multiplexer #(.select(4), .width(8)) multiplexer_6 (
    .in0(register_17_q), .in1(register_20_q), .in2(register_21_q), .in3(register_23_q), .in4(register_25_q),
    .in5(register_28_q), .in6(register_29_q), .in7(register_31_q), .in8(register_32_q), .in9(register_30_q),
    .in10(register_27_q), .in11(register_26_q), .in12(register_24_q), .in13(register_22_q),
    .in14(register_19_q), .in15(register_18_q), .out(multiplexer_6_out), .sel(in_5[3:0]));
  D_Flip_Flop d_ff_3 (.D(or_19_out), .clk(clock_15_out), .Q(out_20), .reset(in_8));  // open: Qn, preset
  and and_52 (and_52_out, or_18_out, out_18);
  assign out_17 = not_30_out ? out_13 : 8'bz;  // Controlled_Buffer controlled_buffer_6
  xor xor_5 (xor_5_out, and_52_out, out_19);
  Hex_Digit_Display hex_digit_display_1 (.value({in_9, out_20, out_19, out_18}));  // open: dp
  Multiplexer #(.select(2), .width(8)) multiplexer_7 (
    .in0(rom_1_data), .in1(out_10), .in2(multiplexer_6_out), .in3(ram_2_dout), .out(out_13), .sel(in_5[5:4]));
  and and_53 (and_53_out, or_18_out, out_18, out_19);
  or or_19 (or_19_out, and_53_out, out_20);

  // Other names for the same wires on the sheet: addr[5:0] = in_5; DATA_IN_RAM[7:0] = in_6; DATA_OUT[7:0] = out_17;
  //   LEITURA0_ESCRITA1 = Entrada_de_dados; R = in_4

  // Notes on the sheet:
  //   Q0
  //   Q1
  //   Q2
  //   Y2
  //   Y2
  //   Y2
  //   Y2
  //   Y2
  //   Y4
  //   Y5
  //   Y5
  //   Y4
  //   Y5
  //   Y4
  //   Y5
  //   Y4
  //   Y5
  //   Y4
  //   Y6
  //   Y6
  //   Y6
  //   Y6
  //   Y6
  //   CS_I/O
  //   OFFSET
  //   CS_RAM
  //   CS_REG
  //   OFFSET
  //   OFFSET
  //   CS_RAM
  //   CS_I/O
  //   00
  //   ADDR[5:0]
  //   A5,A4
  //   Endereço
  //   CS_REG
  //   VALID_L0_WE
  //   WE_L0
  //   01
  //   OFFSET
  //   10
  //   11
  //   CACHE_MISS
  //   Splitter de
  //   endereço
  //   WE_TAG_L0
  //   CACHE_MISS
  //   VALID_L1_WE
  //   CACHE_MISS
  //   VALIDE_L2_WE
  //   CACHE_MISS
  //   VALID_L3_WE
  //   A5,A4
  //   WE_TAG_L1
  //   WE_L1
  //   WE_TAG_L2
  //   WE_L2
  //   WE_TAG_L3
  //   WE_L3
  //   A3..A0
  //   A3..A0
  //   A3..A0
  //   A3..A0
  //   TAG
  //   TAG
  //   TAG
  //   TAG
  //   A3..A0
  //   Indice
  //   WE_BYTE0_L0
  //   WE_BYTE1_L0
  //   Indice
  //   WE_BYTE0_L1
  //   WE_BYTE1_L1
  //   Indice
  //   Indice
  //   WE_BYTE0_L2
  //   WE_BYTE1_L2
  //   WE_BYTE0_L3
  //   WE_BYTE1_L3
  //   Somador de 8 bits
  //   A3..A0
  //   Linha 0
  //   Index_0
  //   Index_1
  //   Linha 2
  //   Index_2
  //   Index_3
  //   Linha 1
  //   Linha 3
  //   DATA_IN[7:0]
  //   Leitura
  //   HIT_L0
  //   HIT_L1
  //   HIT_L2
  //   HIT_L3
  //   Escrita
  //   controlador
  //   de buffer
  //   controlador
  //   de buffer
  //   controlador
  //   de buffer
  //   controlador
  //   de buffer
  //   RAM de Dado
  //   Paridade da RAM
  //   CACHE_MISS
  //   contents of rom_1 (hex, n*v repeats v):
  //   0 a5
  //   Saída de dados L0
  //   Saída de dados L1
  //   CACHE_HIT
  //   Saída de dados L2
  //   Saída de dados L3
  //   ROM
  //   RAM
  //   Registradores
  //   Memória I/O
  //   Ram de paridade
  //   Calculo da paridade
  //   Q0
  //   Led aceso: erro
  //   Q1
  //   AUX I
  //   Q2
  //   DATA_OUT[7:0]
  //   DATA_OUT[7:0]
  //   DATA_OUT[7:0]
  //   DATA_OUT[7:0]
  //   DATA_OUT[7:0]
  //   DATA_OUT[7:0]
  //   CACHE_MIS
  //   AUX II
endmodule
