// Logisim project parte2_cabeada.circ as structural Verilog: 7 circuits, main circuit main
module main (
  input  Reset
);

  wire ALUSrcA, and_1_out, Clk, decoder_7seg_1_a, decoder_7seg_1_b, decoder_7seg_1_c, decoder_7seg_1_d,
       decoder_7seg_1_e, decoder_7seg_1_f, decoder_7seg_1_g, IRWrite, MemRead, or_1_out, PCSource, PCwrite,
       PCWriteCond, RegWrite, uc_1_q0, uc_1_q1, uc_1_q2, ula_1_zero, undriven;
  wire [1:0] OPcode, ulacontrol_1_ulacrt, ULAOp, ULASrcB;
  wire [5:0] IR_q;
  wire [7:0] A_q, B_q, banco_registradores_1_regdata1, banco_registradores_1_regdata2, bit_extender_1_out,
       memory_rom_1_saida, multiplexer_1_out, multiplexer_2_out, PC, PC_q, shifter_1_out, ula_1_ularesult,
       ULAOut;

  Clock clock_1 (.out(Clk));
  Register u_PC (.D(PC), .en(or_1_out), .clk(Clk), .Q(PC_q), .clr(Reset));
  or or_1 (or_1_out, and_1_out, PCwrite);
  UC uc_1 (
    .OPCode(OPcode), .CLK(Clk), .Clear(Reset), .Q0(uc_1_q0), .Q1(uc_1_q1), .Q2(uc_1_q2), .PCSource(PCSource),
    .PCWriteCond(PCWriteCond), .RegWrite(RegWrite), .ULASrcB(ULASrcB), .IRWrite(IRWrite), .MemRead(MemRead),
    .ULAop(ULAOp), .PCWrite(PCwrite), .ALUSrcA(ALUSrcA));
  and and_1 (and_1_out, PCWriteCond, ula_1_zero);
  memory_ROM memory_rom_1 (.Instruction(PC_q), .Saida(memory_rom_1_saida));
  Register IR (.D(memory_rom_1_saida), .en(IRWrite), .clk(Clk), .Q({OPcode, IR_q}), .clr(Reset));
  assign bit_extender_1_out = {{6{IR_q[1]}}, IR_q[1:0]};  // Bit_Extender bit_extender_1
  decoder_7seg decoder_7seg_1 (
    .Q2(uc_1_q2), .Q1(uc_1_q1), .Q0(uc_1_q0), .a(decoder_7seg_1_a), .b(decoder_7seg_1_b),
    .c(decoder_7seg_1_c), .d(decoder_7seg_1_d), .e(decoder_7seg_1_e), .f(decoder_7seg_1_f),
    .g(decoder_7seg_1_g));
  _7_Segment_Display #(.decimalPoint("false")) u_7_segment_display_1 (
    .g(decoder_7seg_1_g), .f(decoder_7seg_1_f), .a(decoder_7seg_1_a), .b(decoder_7seg_1_b),
    .e(decoder_7seg_1_e), .d(decoder_7seg_1_d), .c(decoder_7seg_1_c));
  Shifter shifter_1 (.in(bit_extender_1_out), .\dist (3'b010), .out(shifter_1_out));
  banco_registradores banco_registradores_1 (
    .ReadRegister1(IR_q[5:4]), .ReadRegister2(IR_q[3:2]), .WriteData(ULAOut), .WriteRegister(IR_q[1:0]),
    .RegWrite(RegWrite), .CLOCK(Clk), .CLEAR(undriven), .RegData1(banco_registradores_1_regdata1),
    .RegData2(banco_registradores_1_regdata2));
  Register A (.D(banco_registradores_1_regdata1), .en(Clk), .clk(Clk), .Q(A_q), .clr(Reset));
  Register B (.D(banco_registradores_1_regdata2), .en(Clk), .clk(Clk), .Q(B_q), .clr(Reset));
  Multiplexer #(.width(8)) multiplexer_1 (.in0(PC_q), .in1(A_q), .out(multiplexer_1_out), .sel(ALUSrcA));
  Multiplexer #(.select(2), .width(8)) multiplexer_2 (
    .in0(B_q), .in1(8'h4), .in2(shifter_1_out), .out(multiplexer_2_out), .sel(ULASrcB));  // open: in3
  ULAControl ulacontrol_1 (.ULAOp(ULAOp), .Funct(IR_q[1:0]), .ULACrt(ulacontrol_1_ulacrt));
  ULA ula_1 (
    .A(multiplexer_1_out), .B(multiplexer_2_out), .ULACrt(ulacontrol_1_ulacrt), .ZERO(ula_1_zero),
    .ULAResult(ula_1_ularesult));
  Register u_ULAout (.D(ula_1_ularesult), .clk(Clk), .Q(ULAOut), .clr(Reset));  // open: en
  Multiplexer #(.width(8)) multiplexer_3 (.in0(ula_1_ularesult), .in1(ULAOut), .out(PC), .sel(PCSource));
endmodule

module banco_registradores (
  input  [1:0] ReadRegister1,
  input  [1:0] ReadRegister2,
  input  [7:0] WriteData,
  input  [1:0] WriteRegister,
  input  RegWrite,
  input  CLOCK,
  input  CLEAR,
  output [7:0] RegData1,
  output [7:0] RegData2
);

  wire WE0, WE1, WE2, WE3;
  wire [7:0] demultiplexer_1_out0, demultiplexer_1_out1, demultiplexer_1_out2, demultiplexer_1_out3, Reg0,
       Reg1, Reg2, Reg3;

  Demultiplexer #(.select(2), .width(8)) demultiplexer_1 (
    .out0(demultiplexer_1_out0), .out1(demultiplexer_1_out1), .out2(demultiplexer_1_out2),
    .out3(demultiplexer_1_out3), .in(WriteData), .sel(WriteRegister));
  Demultiplexer #(.select(2)) demultiplexer_2 (
    .out0(WE3), .out1(WE1), .out2(WE2), .out3(WE0), .in(RegWrite), .sel(WriteRegister));
  Register u_Reg3 (.D(demultiplexer_1_out3), .en(WE3), .clk(CLOCK), .Q(Reg3), .clr(CLEAR));
  Register u_Reg0 (.D(demultiplexer_1_out0), .en(WE0), .clk(CLOCK), .Q(Reg0), .clr(CLEAR));
  Register u_Reg1 (.D(demultiplexer_1_out1), .en(WE1), .clk(CLOCK), .Q(Reg1), .clr(CLEAR));
  Register u_Reg2 (.D(demultiplexer_1_out2), .en(WE2), .clk(CLOCK), .Q(Reg2), .clr(CLEAR));
  Multiplexer #(.select(2), .width(8)) multiplexer_1 (
    .in0(Reg0), .in1(Reg1), .in2(Reg2), .in3(Reg3), .out(RegData2), .sel(ReadRegister2));
  Multiplexer #(.select(2), .width(8)) multiplexer_2 (
    .in0(Reg0), .in1(Reg1), .in2(Reg2), .in3(Reg3), .out(RegData1), .sel(ReadRegister1));

  // Other names for the same wires on the sheet: CLK = CLOCK; CLR = CLEAR; Read1[1:0] = ReadRegister1;
  //   Read2[1:0] = ReadRegister2
endmodule

module ULA (
  input  [7:0] A,
  input  [7:0] B,
  input  [1:0] ULACrt,
  output ZERO,
  output [7:0] ULAResult
);

  wire [7:0] adder_1_out, and_1_out, or_1_out, subtractor_1_out;

  Adder adder_1 (.a(A), .b(B), .out(adder_1_out));  // open: cin, cout
  Subtractor subtractor_1 (.a(A), .b(B), .out(subtractor_1_out));  // open: bin, bout
  assign or_1_out = A | B;  // OR_Gate or_1, 8 bits wide
  assign and_1_out = A & B;  // AND_Gate and_1, 8 bits wide
  Multiplexer #(.select(2), .width(8)) multiplexer_1 (
    .in0(adder_1_out), .in1(subtractor_1_out), .in2(or_1_out), .in3(and_1_out), .out(ULAResult), .sel(ULACrt));
  Comparator comparator_1 (.a({8{1'b0}}), .b(ULAResult), .eq(ZERO));  // open: gt, lt
endmodule

module ULAControl (
  input  [1:0] ULAOp,
  input  [1:0] Funct,
  output [1:0] ULACrt
);

  wire and_2_out, and_3_out, not_1_out, not_2_out;

  not not_1 (not_1_out, ULAOp[1]);
  not not_2 (not_2_out, ULAOp[0]);
  and and_1 (ULACrt[1], ULAOp[1], not_2_out, Funct[1]);
  and and_2 (and_2_out, not_1_out, ULAOp[0]);
  and and_3 (and_3_out, ULAOp[1], not_2_out, Funct[0]);
  or or_1 (ULACrt[0], and_2_out, and_3_out);
endmodule

module decoder_7seg (
  input  Q2,
  input  Q1,
  input  Q0,
  output a,
  output b,
  output c,
  output d,
  output e,
  output f,
  output g
);

  wire and_1_out, and_2_out, and_3_out, and_4_out, and_5_out, and_6_out, and_7_out, and_8_out, and_9_out,
       and_10_out, and_11_out, and_12_out, and_13_out, and_14_out, and_15_out, and_16_out, not_1_out,
       not_2_out, not_3_out;

  not not_1 (not_1_out, Q2);
  not not_2 (not_2_out, Q1);
  not not_3 (not_3_out, Q0);
  and and_1 (and_1_out, not_1_out, not_3_out);
  and and_2 (and_2_out, Q2, Q0);
  and and_3 (and_3_out, not_2_out, not_3_out);
  and and_4 (and_4_out, Q1, Q0);
  or or_1 (c, not_2_out, Q0, Q2);
  and and_5 (and_5_out, not_1_out, not_3_out);
  and and_6 (and_6_out, not_1_out, Q1);
  and and_7 (and_7_out, Q2, not_2_out, Q0);
  and and_8 (and_8_out, Q1, not_3_out);
  and and_9 (and_9_out, not_1_out, not_3_out);
  and and_10 (and_10_out, Q1, not_3_out);
  and and_11 (and_11_out, not_2_out, not_3_out);
  and and_12 (and_12_out, Q2, not_2_out);
  and and_13 (and_13_out, Q2, not_3_out);
  and and_14 (and_14_out, not_1_out, Q1);
  and and_15 (and_15_out, Q2, not_2_out);
  and and_16 (and_16_out, Q1, not_3_out);
  or or_2 (a, and_1_out, Q1, and_2_out);
  or or_3 (b, not_1_out, and_3_out, and_4_out);
  or or_4 (d, and_5_out, and_6_out, and_7_out, and_8_out);
  or or_5 (e, and_9_out, and_10_out);
  or or_6 (f, and_11_out, and_12_out, and_13_out);
  or or_7 (g, and_14_out, and_15_out, and_16_out);
endmodule

module memory_ROM (
  input  [7:0] Instruction,
  output [7:0] Saida
);

  ROM rom_1 (.addr(Instruction), .data(Saida));

  // Notes on the sheet:
  //   contents of rom_1 (hex, n*v repeats v):
  //   59
endmodule

module UC (
  input  [1:0] OPCode,
  input  CLK,
  input  Clear,
  output Q0,
  output Q1,
  output Q2,
  output PCSource,
  output PCWriteCond,
  output RegWrite,
  output [1:0] ULASrcB,
  output IRWrite,
  output MemRead,
  output [1:0] ULAop,
  output PCWrite,
  output ALUSrcA
);

  wire and_2_out, and_3_out, and_4_out, and_5_out, D0, D1, D2, nor_1_out, not_1_out, not_2_out, not_3_out,
       not_4_out, not_5_out, not_6_out, not_7_out, not_8_out, not_9_out, not_10_out, not_11_out, not_12_out,
       not_13_out, not_14_out;

  D_Flip_Flop FF0 (.D(D0), .clk(CLK), .Q(Q0), .reset(Clear));  // open: Qn, preset
  D_Flip_Flop FF1 (.D(D1), .clk(CLK), .Q(Q1), .reset(Clear));  // open: Qn, preset
  or or_1 (D0, and_4_out, and_5_out);
  D_Flip_Flop FF2 (.D(D2), .clk(CLK), .Q(Q2), .reset(Clear));  // open: Qn, preset
  or or_2 (D1, and_2_out, and_3_out);
  and and_1 (D2, not_1_out, not_2_out, Q0, not_3_out);
  and and_2 (and_2_out, not_1_out, not_2_out, Q0, nor_1_out);
  and and_3 (and_3_out, not_1_out, Q1, not_4_out);
  and and_4 (and_4_out, not_1_out, not_2_out, not_4_out);
  and and_5 (and_5_out, not_1_out, Q1, not_4_out);
  not not_1 (not_1_out, Q2);
  not not_2 (not_2_out, Q1);
  not not_3 (not_3_out, nor_1_out);
  not not_4 (not_4_out, Q0);
  nor nor_1 (nor_1_out, OPCode[1], OPCode[0]);
  not not_5 (not_5_out, Q2);
  not not_6 (not_6_out, Q2);
  not not_7 (not_7_out, Q1);
  not not_8 (not_8_out, Q0);
  and S0 (IRWrite, not_5_out, not_7_out, not_8_out);
  not not_9 (not_9_out, Q1);
  not not_10 (not_10_out, Q2);
  and S1 (ULASrcB[0], not_6_out, not_9_out, Q0);
  and S2 (ULAop[1], not_10_out, Q1, not_11_out);
  not not_11 (not_11_out, Q0);
  not not_12 (not_12_out, Q2);
  and S3 (RegWrite, not_12_out, Q1, Q0);
  or or_3 (ALUSrcA, ULAop[1], PCSource);
  not not_13 (not_13_out, Q1);
  not not_14 (not_14_out, Q0);
  and S4 (PCSource, Q2, not_13_out, not_14_out);

  assign MemRead = IRWrite;
  assign PCWrite = IRWrite;
  assign PCWriteCond = PCSource;
  assign ULAop[0] = PCSource;
  assign ULASrcB[1] = IRWrite;

  // Other names for the same wires on the sheet: Reset = Clear
endmodule
