// Logisim project parte2_microprograma.circ as structural Verilog: 6 circuits, main circuit main
module main (
  input  Reset
);

  wire ALUSrcA, and_1_out, Clk, decoder_7seg_1_p1, decoder_7seg_1_p2, decoder_7seg_1_p3, decoder_7seg_1_p4,
       decoder_7seg_1_p5, decoder_7seg_1_p6, decoder_7seg_1_p7, decoder_7seg_1_p8, decoder_7seg_1_p9,
       decoder_7seg_1_p10, IRWrite, MemRead, or_1_out, PCSource, PCwrite, PCWriteCond, RegWrite, ula_1_zero,
       undriven;
  wire [1:0] OPcode, ulacontrol_1_ulacrt, ULAOp, ULASrcB;
  wire [5:0] IR_q;
  wire [7:0] A_q, B_q, banco_registradores_1_regdata1, banco_registradores_1_regdata2, bit_extender_1_out,
       memory_rom_1_saida, multiplexer_1_out, multiplexer_2_out, PC, PC_q, shifter_1_out, ula_1_ularesult,
       ULAOut;

  Clock clock_1 (.out(Clk));
  Register u_PC (.D(PC), .en(or_1_out), .clk(Clk), .Q(PC_q), .clr(Reset));
  or or_1 (or_1_out, and_1_out, PCwrite);
  // decoder_7seg decoder_7seg_1: pin names not known; wires that end beside it: decoder_7seg_1_p1, decoder_7seg_1_p2, decoder_7seg_1_p3, decoder_7seg_1_p4, decoder_7seg_1_p5, decoder_7seg_1_p6, decoder_7seg_1_p7, decoder_7seg_1_p8, decoder_7seg_1_p9, decoder_7seg_1_p10, decoder_7seg_1_p1
  and and_1 (and_1_out, PCWriteCond, ula_1_zero);
  memory_rom memory_rom_1 (.Instruction(PC_q), .Enable(MemRead), .Saida(memory_rom_1_saida));
  Register IR (.D(memory_rom_1_saida), .en(IRWrite), .clk(Clk), .Q({OPcode, IR_q}), .clr(Reset));
  _7_Segment_Display u_7_segment_display_1 (
    .g(decoder_7seg_1_p10), .f(decoder_7seg_1_p9), .a(decoder_7seg_1_p4), .b(decoder_7seg_1_p5),
    .e(decoder_7seg_1_p8), .d(decoder_7seg_1_p7), .c(decoder_7seg_1_p6));  // open: dp
  UC uc_1 (
    .OPCode(OPcode), .Clear(Reset), .CLK(Clk), .Q0(decoder_7seg_1_p1), .Q2(decoder_7seg_1_p3),
    .Q1(decoder_7seg_1_p2), .ULAOp(ULAOp), .PCWrite(PCwrite), .ALUSrcA(ALUSrcA), .ULASrcB(ULASrcB),
    .MemRead(MemRead), .IRWrite(IRWrite), .RegWrite(RegWrite), .PCSource(PCSource), .PCWriteCond(PCWriteCond));
  assign bit_extender_1_out = {{6{IR_q[1]}}, IR_q[1:0]};  // Bit_Extender bit_extender_1
  Shifter shifter_1 (.in(bit_extender_1_out), .\dist (3'b010), .out(shifter_1_out));
  banco_registradores banco_registradores_1 (
    .ReadRegister1(IR_q[5:4]), .ReadRegister2(IR_q[3:2]), .WriteData(ULAOut), .WriteRegister(IR_q[1:0]),
    .RegWrite(RegWrite), .CLOCK(Clk), .CLEAR(undriven), .RegData1(banco_registradores_1_regdata1),
    .RegData2(banco_registradores_1_regdata2));
  Register A (.D(banco_registradores_1_regdata1), .en(Clk), .clk(Clk), .Q(A_q), .clr(Reset));
  Register B (.D(banco_registradores_1_regdata2), .en(Clk), .clk(Clk), .Q(B_q), .clr(Reset));
  Multiplexer #(.width(8)) multiplexer_1 (.in0(A_q), .in1(PC_q), .out(multiplexer_1_out), .sel(ALUSrcA));
  Multiplexer #(.select(2), .width(8)) multiplexer_2 (
    .in0(B_q), .in1(8'h4), .in2(shifter_1_out), .out(multiplexer_2_out), .sel(ULASrcB));  // open: in3
  ULAControl ulacontrol_1 (.ULAOp(ULAOp), .Funct(IR_q[1:0]), .ULACrt(ulacontrol_1_ulacrt));
  ULA ula_1 (
    .A(multiplexer_1_out), .B(multiplexer_2_out), .ULACrt(ulacontrol_1_ulacrt), .ZERO(ula_1_zero),
    .ULAResult(ula_1_ularesult));
  Register u_ULAout (.D(ula_1_ularesult), .clk(Clk), .Q(ULAOut), .clr(Reset));  // open: en
  Multiplexer #(.width(8)) multiplexer_3 (.in0(ula_1_ularesult), .in1(ULAOut), .out(PC), .sel(PCSource));
endmodule

module banco_registradores (
  input  [1:0] ReadRegister1,
  input  [1:0] ReadRegister2,
  input  [7:0] WriteData,
  input  [1:0] WriteRegister,
  input  RegWrite,
  input  CLOCK,
  input  CLEAR,
  output [7:0] RegData1,
  output [7:0] RegData2
);

  wire WE0, WE1, WE2, WE3;
  wire [7:0] demultiplexer_1_out0, demultiplexer_1_out1, demultiplexer_1_out2, demultiplexer_1_out3, Reg0,
       Reg1, Reg2, Reg3;

  Demultiplexer #(.select(2), .width(8)) demultiplexer_1 (
    .out0(demultiplexer_1_out0), .out1(demultiplexer_1_out1), .out2(demultiplexer_1_out2),
    .out3(demultiplexer_1_out3), .in(WriteData), .sel(WriteRegister));
  Demultiplexer #(.select(2)) demultiplexer_2 (
    .out0(WE3), .out1(WE1), .out2(WE2), .out3(WE0), .in(RegWrite), .sel(WriteRegister));
  Register u_Reg3 (.D(demultiplexer_1_out3), .en(WE3), .clk(CLOCK), .Q(Reg3), .clr(CLEAR));
  Register u_Reg0 (.D(demultiplexer_1_out0), .en(WE0), .clk(CLOCK), .Q(Reg0), .clr(CLEAR));
  Register u_Reg1 (.D(demultiplexer_1_out1), .en(WE1), .clk(CLOCK), .Q(Reg1), .clr(CLEAR));
  Register u_Reg2 (.D(demultiplexer_1_out2), .en(WE2), .clk(CLOCK), .Q(Reg2), .clr(CLEAR));
  Multiplexer #(.select(2), .width(8)) multiplexer_1 (
    .in0(Reg0), .in1(Reg1), .in2(Reg2), .in3(Reg3), .out(RegData2), .sel(ReadRegister2));
  Multiplexer #(.select(2), .width(8)) multiplexer_2 (
    .in0(Reg0), .in1(Reg1), .in2(Reg2), .in3(Reg3), .out(RegData1), .sel(ReadRegister1));

  // Other names for the same wires on the sheet: CLK = CLOCK; CLR = CLEAR; Read1[1:0] = ReadRegister1;
  //   Read2[1:0] = ReadRegister2
endmodule

module ULA (
  input  [7:0] A,
  input  [7:0] B,
  input  [1:0] ULACrt,
  output ZERO,
  output [7:0] ULAResult
);

  wire [7:0] adder_1_out, and_1_out, or_1_out, subtractor_1_out;

  Subtractor subtractor_1 (.a(A), .b(B), .out(subtractor_1_out));  // open: bin, bout
  Adder adder_1 (.a(A), .b(B), .out(adder_1_out));  // open: cin, cout
  assign or_1_out = A | B;  // OR_Gate or_1, 8 bits wide
  assign and_1_out = A & B;  // AND_Gate and_1, 8 bits wide
  Multiplexer #(.select(2), .width(8)) multiplexer_1 (
    .in0(subtractor_1_out), .in1(adder_1_out), .in2(or_1_out), .in3(and_1_out), .out(ULAResult), .sel(ULACrt));
  Comparator comparator_1 (.a({8{1'b0}}), .b(ULAResult), .eq(ZERO));  // open: gt, lt
endmodule

module ULAControl (
  input  [1:0] ULAOp,
  input  [1:0] Funct,
  output [1:0] ULACrt
);

  wire and_2_out, and_3_out, not_1_out, not_2_out;

  not not_1 (not_1_out, ULAOp[1]);
  not not_2 (not_2_out, ULAOp[0]);
  and and_1 (ULACrt[1], ULAOp[1], not_2_out, Funct[1]);
  and and_2 (and_2_out, not_1_out, ULAOp[0]);
  and and_3 (and_3_out, ULAOp[1], not_2_out, Funct[0]);
  or or_1 (ULACrt[0], and_2_out, and_3_out);
endmodule

module memory_rom (
  input  [7:0] Instruction,
  input  Enable,
  output [7:0] Saida
);

  ROM rom_1 (.addr(Instruction), .data(Saida));

  // Notes on the sheet:
  //   contents of rom_1 (hex, n*v repeats v):
  //   59
endmodule

module UC (
  input  [1:0] OPCode,
  input  Clear,
  input  CLK,
  output Q0,
  output Q2,
  output Q1,
  output [1:0] ULAOp,
  output PCWrite,
  output ALUSrcA,
  output [1:0] ULASrcB,
  output MemRead,
  output IRWrite,
  output RegWrite,
  output PCSource,
  output PCWriteCond
);

  wire nor_1_out;
  wire [2:0] adder_1_out, multiplexer_1_out, multiplexer_2_out;
  wire [5:0] rom_1_data;

  Counter #(.max('h7), .width(3)) counter_1 (
    .clr(Clear), .clk(CLK), .D(multiplexer_1_out), .Q({Q0, Q1, Q2}));  // open: load, up, count, carry
  ROM #(.addrWidth(3)) rom_1 (.addr({Q0, Q1, Q2}), .data({ULAOp, rom_1_data}));
  Adder #(.width(3)) adder_1 (.a({Q0, Q1, Q2}), .b(3'b001), .out(adder_1_out));  // open: cin, cout
  Decoder #(.enable("false"), .select(2)) decoder_1 (
    .out0(RegWrite), .out1(IRWrite), .out3(PCSource), .sel(rom_1_data[3:2]));  // open: out2
  Multiplexer #(.select(2), .width(3)) multiplexer_1 (
    .in0(adder_1_out), .in1(3'b000), .in2(multiplexer_2_out), .in3(3'b000), .out(multiplexer_1_out));  // open: sel
  nor nor_1 (nor_1_out, OPCode[1], OPCode[0]);
  Multiplexer #(.width(3)) multiplexer_2 (.in0(3'b100), .in1(3'b010), .out(multiplexer_2_out), .sel(nor_1_out));
  Decoder #(.enable("false"), .select(2)) decoder_2 (
    .out0(PCWrite), .out1(ALUSrcA), .out3(ULASrcB[1]), .sel(rom_1_data[5:4]));  // open: out2

  assign MemRead = IRWrite;
  assign PCWriteCond = PCSource;
  assign ULASrcB[0] = PCWrite;

  // Notes on the sheet:
  //   contents of rom_1 (hex, n*v repeats v):
  //   76 32 2e 6f 20 72 61 77
endmodule
